# Fritzing sketch arduino (saved by Fritzing 1.0.1rc)

parts:
  Part1 = RFID-RC522-v2
  HC-SR04_Sensor_1 = HC-SR04 Ultrasonic Distance Sensor
  J1 = Piezo Speaker
  Part2 = Arduino Uno (Rev3)
  ENC28J2 = ENC28J60

nets:
  N1: Part1.SDA, Part2.D4
  GND: Part1.GND, HC-SR04_Sensor_1.GND, Part2.GND, ENC28J2.GND
  N2: Part1.RST, Part2.D5_PWM
  3.3V: Part1.3.3V, Part2.3V3
  N3: HC-SR04_Sensor_1.TRIG, Part2.D7
  N4: HC-SR04_Sensor_1.ECHO, Part2.D6_PWM
  N5: J1.pin2, Part2.D3_PWM
  5V: Part2.D10_PWM/SS, Part2.5V, ENC28J2.CS, ENC28J2.VCC
  N6: Part2.D11_PWM/MOSI, ENC28J2.SI
  N7: Part2.D12/MISO, ENC28J2.SO
  N8: Part2.D13/SCK, ENC28J2.SCK
  N9: Part2.RESET, ENC28J2.RST

notes:
  COLORS
  GND = blue
  power = red
  reset = white
  SPI
  SCK = green
  SO/MISO = yellow
  SI/MOSI = orange
  CS/SS/SDA = brown
  ultrasonic trig, echo; buzzer = gray
  purple = not used
  ENC28J60
  CLK - INT
  WOL - SO/MISO
  SI/MOSI - SCK
  CS - RST
  VCC - GND
  SPI
  SCK = 13
  MOSI/SI = 11
  MISO/SO = 12
  ISCP
  MISO - VCC
  SCK - MOSI
  RESET - GND
  Wrong colors
  comp - correct - actual
  buzzer - gray - white
  buzzer - blue - black
  rfid - green - gray
  rfid - orange - black

custom parts:
  RFID-RC522-v2: A simple China made RFID-RC522 Reader; do check the pin labels, as this is a MFRC522 based clone.
  ENC28J60: Ethernet Module ENC28J60
