# Fritzing sketch raspberrypi (saved by Fritzing 1.0.1rc)
breadboards: 1

parts:
  Raspberry_Pi_1 = Raspberry Pi 3 [part_number=RPI-3-V1.2]
  HC-SR04_Sensor_1 = HC-SR04 Ultrasonic Distance Sensor
  J1 = Piezo Speaker
  R1 = Resistor [tolerance=±5% resistance=220 package="1206 [SMD]"]
  R2 = Resistor [tolerance=±5% resistance=220 package="1206 [SMD]"]

nets:
  GND: Raspberry_Pi_1.GND, HC-SR04_Sensor_1.GND, J1.pin1, R2.Pin_1
  N1: Raspberry_Pi_1.GIPO24, R1.Pin_1, R2.Pin_0
  N2: Raspberry_Pi_1.GIPO23, HC-SR04_Sensor_1.TRIG
  N3: Raspberry_Pi_1.GIPO18, J1.pin2
  5V: Raspberry_Pi_1.5V, HC-SR04_Sensor_1.VCC
  N4: HC-SR04_Sensor_1.ECHO, R1.Pin_0
